# Fritzing sketch Untitled_Sketch (saved by Fritzing 0.9.3b)

parts:
  TRS1 = Audio Jack (TRS) 3.5mm [package="PG203J [THT]"]
  Composant1 = Arduino Mega 2560 (Rev3)
  Composant2 = Base Shield V2
  Grove1 = Grove OLED 128x96
  Composant3 = FONA 800 Shield
  Grove2 = Grove-I2C
  Grove3 = Grove Button
  Grove4 = Grove Button
  Grove_Switch_(P)1 = Grove Switch (P)
  Grove_Switch_(P)2 = Grove Switch (P)
  Composant5 = Memoire 1.0 - SD card log shield
  U1 = 4-Channel 5v Relay Shield [package=relay-4ch5v10a]

nets:
  GND: TRS1.Sleeve, Composant1.GND, Grove2.GND
  N1: TRS1.Ring, TRS1.Tip, Composant1.D46
  N2: Composant1.A0, U1.IN4
  N3: Composant1.D21/SCL, Grove2.SCL
  N4: Composant1.D20/SDA, Grove2.SDA
  N5: Composant1.D15/RX3, Composant3.D3
  N6: Composant1.D14/TX3, Composant3.D2
  VCC: Composant1.5V, Grove1.VCC, Grove2.VCC
  N7: Composant2.A1, U1.IN3
  N8: Composant2.A2, U1.IN2
  N9: Composant2.A3, U1.IN1
  GND_2: Composant2.GND, Grove1.GND, U1.GND
  N10: Composant2.A4, Grove1.SCL
  N11: Composant2.A5, Grove1.SDA
  N12: Composant2.D4, Composant5.DIG_4
  5V: Composant2.5V, U1.VCC
  N13: Composant2.pin_108, Grove3.GND
  N14: Composant2.pin_109, Grove3.VCC
  N15: Composant2.pin_110, Grove3.NC
  N16: Composant2.pin_111, Grove3.SIG
  N17: Composant2.pin_112, Grove4.GND
  N18: Composant2.pin_113, Grove4.VCC
  N19: Composant2.pin_114, Grove4.NC
  N20: Composant2.pin_115, Grove4.SIG
  N21: Composant2.pin_116, Grove_Switch_(P)1.GND
  N22: Composant2.pin_117, Grove_Switch_(P)1.VCC
  N23: Composant2.pin_118, Grove_Switch_(P)1.NC
  N24: Composant2.pin_119, Grove_Switch_(P)1.SIG
  N25: Composant2.pin_120, Grove_Switch_(P)2.GND
  N26: Composant2.pin_121, Grove_Switch_(P)2.VCC
  N27: Composant2.pin_122, Grove_Switch_(P)2.NC
  N28: Composant2.pin_123, Grove_Switch_(P)2.SIG

custom parts:
  FONA 800 Shield: This shield fits on top of any classic Arduino or compatible, and packs a surprising amount of technology into it's little frame. At the heart is a GSM cellular module (we use the latest SIM800) the size of a postage stamp. Quad-band 850/900/1800/1900MHz - connect onto any global GSM network with any 2G SIM (in the USA, T-Mobile is suggested) Make and receive voice calls using a headset OR an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
  Grove Switch (P): Switch, Grove connector, panel mount.
  4-Channel 5v Relay Shield: 4 Channel 5v Relay Shield w. 2x SPD-06VDC-SD-C
